// Logisim project BuildingBlocks.circ as structural Verilog: 5 circuits, main circuit main
module main (
  input  A,
  input  B,
  input  ENABLE,
  output out_4,
  output out_5,
  output out_6,
  output out_7
);

  wire not_1_out, not_2_out;

  not not_1 (not_1_out, A);
  not not_2 (not_2_out, B);
  and and_1 (out_4, not_1_out, not_2_out, ENABLE);
  and and_2 (out_5, A, not_2_out, ENABLE);
  and and_3 (out_6, B, not_1_out, ENABLE);
  and and_4 (out_7, B, A, ENABLE);
endmodule

module _2_to_4_Decoder (
  input  A,
  input  B,
  input  ENABLE,
  output out_4,
  output out_5,
  output out_6,
  output out_7
);

  wire not_1_out, not_2_out;

  not not_1 (not_1_out, A);
  not not_2 (not_2_out, B);
  and _00 (out_4, not_1_out, not_2_out, ENABLE);
  and _10 (out_5, A, not_2_out, ENABLE);
  and _01 (out_6, B, not_1_out, ENABLE);
  and and_1 (out_7, B, A, ENABLE);
endmodule

module _8_to_1_Multiplexer (
  input  D0,
  input  D1,
  input  D2,
  input  D3,
  input  D4,
  input  D5,
  input  D6,
  input  D7,
  input  A,
  input  B,
  input  C,
  output F
);

  wire and_1_out, and_2_out, and_3_out, and_4_out, and_5_out, and_6_out, and_7_out, and_8_out, not_1_out,
       not_2_out, not_3_out;

  not not_1 (not_1_out, B);
  not not_2 (not_2_out, A);
  not not_3 (not_3_out, C);
  and and_1 (and_1_out, D0, not_2_out, not_1_out, not_3_out);
  and and_2 (and_2_out, D1, not_2_out, not_1_out, C);
  and and_3 (and_3_out, D2, not_2_out, B, not_3_out);
  and and_4 (and_4_out, D3, not_2_out, B, C);
  and and_5 (and_5_out, D4, A, not_1_out, not_3_out);
  and and_6 (and_6_out, D5, A, not_1_out, C);
  and and_7 (and_7_out, D6, A, B, not_3_out);
  and and_8 (and_8_out, D7, A, B, C);
  or or_1 (F, and_1_out, and_2_out, and_3_out, and_4_out, and_5_out, and_6_out, and_7_out, and_8_out);

  // Notes on the sheet:
  //   A
  //   _
  //   _
  //   A
  //   B
  //   B
  //   _
  //   C
  //   C
endmodule

module _8_bit_Comparator (
  input  A3,
  input  A2,
  input  A1,
  input  A0,
  input  A3_2,
  input  A2_2,
  input  A1_2,
  input  A0_2,
  input  B3,
  input  B2,
  input  B1,
  input  B0,
  input  B3_2,
  input  B2_2,
  input  B1_2,
  input  B0_2,
  output X
);

  wire xnor_1_out, xnor_4_out, xnor_5_out, xnor_6_out, xnor_7_out, xnor_8_out;

  xnor xnor_1 (xnor_1_out, A0_2, B0_2);
  xnor xnor_2 (xnor_1_out, A1_2, B1_2);
  xnor xnor_3 (xnor_1_out, A2_2, B2_2);
  xnor xnor_4 (xnor_4_out, A3_2, B3_2);
  xnor xnor_5 (xnor_5_out, A0, B0);
  xnor xnor_6 (xnor_6_out, A1, B1);
  xnor xnor_7 (xnor_7_out, A2, B2);
  xnor xnor_8 (xnor_8_out, A3, B3);
  and and_1 (X, xnor_1_out, xnor_1_out, xnor_1_out, xnor_4_out, xnor_5_out, xnor_6_out, xnor_7_out, xnor_8_out);
endmodule

module _8_bit_wide__1_bit_left_right_shifter (
  input  D0,
  input  D1,
  input  D2,
  input  D3,
  input  D4,
  input  D5,
  input  D6,
  input  D7,
  input  in_9,
  output S0,
  output S1,
  output S2,
  output S3,
  output S4,
  output S5,
  output S6,
  output S7
);

  wire and_1_out, and_3_out, and_4_out, and_5_out, and_6_out, and_7_out, and_8_out, and_9_out, and_10_out,
       and_11_out, and_12_out, and_14_out, not_1_out;

  not not_1 (not_1_out, in_9);
  and and_1 (and_1_out, D0, in_9);
  and and_2 (S0, not_1_out, D1);
  or or_1 (S1, and_1_out, and_5_out);
  and and_3 (and_3_out, D1, in_9);
  and and_4 (and_4_out, D2, in_9);
  and and_5 (and_5_out, not_1_out, D2);
  or or_2 (S2, and_3_out, and_6_out);
  and and_6 (and_6_out, not_1_out, D3);
  and and_7 (and_7_out, D3, in_9);
  or or_3 (S3, and_4_out, and_8_out);
  and and_8 (and_8_out, not_1_out, D4);
  and and_9 (and_9_out, D4, in_9);
  or or_4 (S4, and_7_out, and_10_out);
  and and_10 (and_10_out, not_1_out, D5);
  and and_11 (and_11_out, D5, in_9);
  or or_5 (S5, and_9_out, and_12_out);
  and and_12 (and_12_out, not_1_out, D6);
  and and_13 (S7, D6, in_9);
  or or_6 (S6, and_11_out, and_14_out);
  and and_14 (and_14_out, not_1_out, D7);
endmodule
