// Logisim project DLL8-ALU.circ as structural Verilog: 9 circuits, main circuit main
module main (
);

  ALU alu_1 ();  // open: ENB, ENA, INVA, Carry_In, F1, Clk, F0, B7, B6, B5, B4, B3, B2, B1, B0, A7, A6, A5, A4, A3, A2, A1, A0, out_25, out_26, out_27, out_28, out_29, out_30, out_31, out_32, Carry_Out
endmodule

module _8_bit_Ripple_Carry_Adder (
  input  A7,
  input  A6,
  input  A5,
  input  A4,
  input  A3,
  input  A2,
  input  A1,
  input  A0,
  input  B7,
  input  B6,
  input  B5,
  input  B4,
  input  B3,
  input  B2,
  input  B1,
  input  B0,
  input  C_IN,
  output out_18,
  output out_19,
  output out_20,
  output out_21,
  output out_22,
  output out_23,
  output out_24,
  output out_25,
  output out_26
);

  wire fulladder_2_c_out, fulladder_3_c_out, fulladder_4_c_out, fulladder_5_c_out, fulladder_6_c_out,
       fulladder_7_c_out, fulladder_8_c_out;

  FullAdder fulladder_1 (.A(A7), .B(B7), .C(fulladder_2_c_out), .S(out_19), .C_OUT(out_18));
  FullAdder fulladder_2 (.A(A6), .B(B6), .C(fulladder_3_c_out), .S(out_20), .C_OUT(fulladder_2_c_out));
  FullAdder fulladder_3 (.A(A5), .B(B5), .C(fulladder_4_c_out), .S(out_21), .C_OUT(fulladder_3_c_out));
  FullAdder fulladder_4 (.A(A4), .B(B4), .C(fulladder_5_c_out), .S(out_22), .C_OUT(fulladder_4_c_out));
  FullAdder fulladder_5 (.A(A3), .B(B3), .C(fulladder_6_c_out), .S(out_23), .C_OUT(fulladder_5_c_out));
  FullAdder fulladder_6 (.A(A2), .B(B2), .C(fulladder_7_c_out), .S(out_24), .C_OUT(fulladder_6_c_out));
  FullAdder fulladder_7 (.A(A1), .B(B1), .C(fulladder_8_c_out), .S(out_25), .C_OUT(fulladder_7_c_out));
  FullAdder fulladder_8 (.A(A0), .B(B0), .C(C_IN), .S(out_26), .C_OUT(fulladder_8_c_out));
endmodule

module HalfAdder (
  input  in_1,
  input  in_2,
  output out_3,
  output out_4
);

  xor xor_1 (out_3, in_1, in_2);
  buf and_1 (out_4, in_1);  // AND_Gate
endmodule

module FullAdder (
  input  A,
  input  B,
  input  C,
  output S,
  output C_OUT
);

  wire and_1_out, and_2_out, xor_1_out;

  xor xor_1 (xor_1_out, A, B);
  xor xor_2 (S, xor_1_out, C);
  and and_1 (and_1_out, xor_1_out, C);
  and and_2 (and_2_out, A, B);
  or or_1 (C_OUT, and_1_out, and_2_out);
endmodule

module _8_bit_Bitwise_AND (
  input  A7,
  input  A6,
  input  A5,
  input  A4,
  input  A3,
  input  A2,
  input  A1,
  input  A0,
  input  B7,
  input  B6,
  input  B5,
  input  B4,
  input  B3,
  input  B2,
  input  B1,
  input  B0,
  output _07,
  output _06,
  output _05,
  output _04,
  output _03,
  output _02,
  output _01,
  output _00
);

  and _7 (_07, A7, B7);
  and _6 (_06, A6, B6);
  and _5 (_05, A5, B5);
  and _4 (_04, A4, B4);
  and _3 (_03, A3, B3);
  and _2 (_02, A2, B2);
  and _1 (_01, A1, B1);
  and _0 (_00, A0, B0);
endmodule

module _8_bit_Bitwise_NOT (
  input  A7,
  input  A6,
  input  A5,
  input  A4,
  input  A3,
  input  A2,
  input  A1,
  input  A0,
  output _07,
  output _06,
  output _05,
  output _04,
  output out_13,
  output out_14,
  output out_15,
  output out_16
);

  not _7 (_07, A7);
  not _6 (_06, A6);
  not _5 (_05, A5);
  not _4 (_04, A4);
  not _3 (out_13, A3);
  not _2 (out_14, A2);
  not _1 (out_15, A1);
  not _0 (out_16, A0);
endmodule

module _8_bit_Bitwise_OR (
  input  A7,
  input  A6,
  input  A5,
  input  A4,
  input  A3,
  input  A2,
  input  A1,
  input  A0,
  input  B7,
  input  B6,
  input  B5,
  input  B4,
  input  B3,
  input  B2,
  input  B1,
  input  B0,
  output _07,
  output _06,
  output _05,
  output _04,
  output out_21,
  output out_22,
  output out_23,
  output out_24
);

  or _7 (_07, A7, B7);
  or _6 (_06, A6, B6);
  or _5 (_05, A5, B5);
  or _4 (_04, A4, B4);
  or _3 (out_21, A3, B3);
  or _2 (out_22, A2, B2);
  or _1 (out_23, A1, B1);
  or _0 (out_24, A0, B0);
endmodule

module ALU (
  input  B7,
  input  B6,
  input  B5,
  input  B4,
  input  B3,
  input  B2,
  input  B1,
  input  B0,
  input  A7,
  input  A6,
  input  A5,
  input  A4,
  input  A3,
  input  A2,
  input  A1,
  input  A0,
  input  ENB,
  input  ENA,
  input  INVA,
  input  Carry_In,
  input  F1,
  input  F0,
  input  Clk,
  output Carry_Out,
  output out_25,
  output out_26,
  output out_27,
  output out_28,
  output out_29,
  output out_30,
  output out_31,
  output out_32
);

  wire n2_to_4_decoder_1_out_4, n2_to_4_decoder_1_out_5, n2_to_4_decoder_1_out_6, n2_to_4_decoder_1_out_7,
       not_1_out, not_2_out, not_3_out;
  wire [7:0] AND__07, controlled_buffer_1_out, controlled_buffer_4_out, controlled_buffer_6_out,
       n8_bit_bitwise_not_1__07, n8_bit_bitwise_or_1__07, Ripple_Adder_out_26;

  assign controlled_buffer_1_out = not_2_out ? {8{ENB}} : 8'bz;  // Controlled_Buffer controlled_buffer_1
  not not_1 (not_1_out, ENA);
  not not_2 (not_2_out, ENB);
  _2__to_4_Decoder u_2_to_4_decoder_1 (
    .A(F1), .B(F0), .ENABLE(Clk), .out_4(n2_to_4_decoder_1_out_4), .out_5(n2_to_4_decoder_1_out_5),
    .out_6(n2_to_4_decoder_1_out_6), .out_7(n2_to_4_decoder_1_out_7));
  assign controlled_buffer_1_out = ENB ? {B7, B6, B5, B4, B3, B2, B1, B0} : 8'bz;  // Controlled_Buffer controlled_buffer_2
  _8_bit_Bitwise_AND AND (
    .A7(controlled_buffer_6_out[0]), .A6(controlled_buffer_6_out[1]), .A5(controlled_buffer_6_out[2]),
    .A4(controlled_buffer_6_out[3]), .A3(controlled_buffer_6_out[4]), .A2(controlled_buffer_6_out[5]),
    .A1(controlled_buffer_6_out[6]), .A0(controlled_buffer_6_out[7]), .B7(controlled_buffer_1_out[0]),
    .B6(controlled_buffer_1_out[1]), .B5(controlled_buffer_1_out[2]), .B4(controlled_buffer_1_out[3]),
    .B3(controlled_buffer_1_out[4]), .B2(controlled_buffer_1_out[5]), .B1(controlled_buffer_1_out[6]),
    .B0(controlled_buffer_1_out[7]), ._07(AND__07[0]), ._06(AND__07[1]), ._05(AND__07[2]), ._04(AND__07[3]),
    ._03(AND__07[4]), ._02(AND__07[5]), ._01(AND__07[6]), ._00(AND__07[7]));
  assign {out_25, out_26, out_27, out_28, out_29, out_30, out_31, out_32} = n2_to_4_decoder_1_out_4 ? AND__07 : 8'bz;  // Controlled_Buffer controlled_buffer_3
  not not_3 (not_3_out, INVA);
  _8_bit_Bitwise_OR u_8_bit_bitwise_or_1 (
    .A7(controlled_buffer_6_out[0]), .A6(controlled_buffer_6_out[1]), .A5(controlled_buffer_6_out[2]),
    .A4(controlled_buffer_6_out[3]), .A3(controlled_buffer_6_out[4]), .A2(controlled_buffer_6_out[5]),
    .A1(controlled_buffer_6_out[6]), .A0(controlled_buffer_6_out[7]), .B7(controlled_buffer_1_out[0]),
    .B6(controlled_buffer_1_out[1]), .B5(controlled_buffer_1_out[2]), .B4(controlled_buffer_1_out[3]),
    .B3(controlled_buffer_1_out[4]), .B2(controlled_buffer_1_out[5]), .B1(controlled_buffer_1_out[6]),
    .B0(controlled_buffer_1_out[7]), ._07(n8_bit_bitwise_or_1__07[0]), ._06(n8_bit_bitwise_or_1__07[1]),
    ._05(n8_bit_bitwise_or_1__07[2]), ._04(n8_bit_bitwise_or_1__07[3]), .out_21(n8_bit_bitwise_or_1__07[4]),
    .out_22(n8_bit_bitwise_or_1__07[5]), .out_23(n8_bit_bitwise_or_1__07[6]),
    .out_24(n8_bit_bitwise_or_1__07[7]));
  assign controlled_buffer_4_out = ENA ? {A7, A6, A5, A4, A3, A2, A1, A0} : 8'bz;  // Controlled_Buffer controlled_buffer_4
  assign controlled_buffer_4_out = not_1_out ? {8{ENA}} : 8'bz;  // Controlled_Buffer controlled_buffer_5
  assign controlled_buffer_6_out = not_3_out ? controlled_buffer_4_out : 8'bz;  // Controlled_Buffer controlled_buffer_6
  assign {out_25, out_26, out_27, out_28, out_29, out_30, out_31, out_32} = n2_to_4_decoder_1_out_5 ? n8_bit_bitwise_or_1__07 : 8'bz;  // Controlled_Buffer controlled_buffer_7
  assign controlled_buffer_6_out = INVA ? ~controlled_buffer_4_out : 8'bz;  // Controlled_Inverter controlled_inverter_1
  _8_bit_Bitwise_NOT u_8_bit_bitwise_not_1 (
    .A7(controlled_buffer_1_out[0]), .A6(controlled_buffer_1_out[1]), .A5(controlled_buffer_1_out[2]),
    .A4(controlled_buffer_1_out[3]), .A3(controlled_buffer_1_out[4]), .A2(controlled_buffer_1_out[5]),
    .A1(controlled_buffer_1_out[6]), .A0(controlled_buffer_1_out[7]), ._07(n8_bit_bitwise_not_1__07[0]),
    ._06(n8_bit_bitwise_not_1__07[1]), ._05(n8_bit_bitwise_not_1__07[2]), ._04(n8_bit_bitwise_not_1__07[3]),
    .out_13(n8_bit_bitwise_not_1__07[4]), .out_14(n8_bit_bitwise_not_1__07[5]),
    .out_15(n8_bit_bitwise_not_1__07[6]), .out_16(n8_bit_bitwise_not_1__07[7]));
  assign {out_25, out_26, out_27, out_28, out_29, out_30, out_31, out_32} = n2_to_4_decoder_1_out_6 ? n8_bit_bitwise_not_1__07 : 8'bz;  // Controlled_Buffer controlled_buffer_8
  _8_bit_Ripple_Carry_Adder Ripple_Adder (
    .out_18(Carry_Out), .A7(controlled_buffer_1_out[7]), .A6(controlled_buffer_1_out[6]),
    .A5(controlled_buffer_1_out[5]), .A4(controlled_buffer_1_out[4]), .A3(controlled_buffer_1_out[3]),
    .A2(controlled_buffer_1_out[2]), .A1(controlled_buffer_1_out[1]), .A0(controlled_buffer_1_out[0]),
    .B7(controlled_buffer_6_out[7]), .B6(controlled_buffer_6_out[6]), .B5(controlled_buffer_6_out[5]),
    .B4(controlled_buffer_6_out[4]), .B3(controlled_buffer_6_out[3]), .B2(controlled_buffer_6_out[2]),
    .B1(controlled_buffer_6_out[1]), .B0(controlled_buffer_6_out[0]), .out_19(Ripple_Adder_out_26[7]),
    .out_20(Ripple_Adder_out_26[6]), .out_21(Ripple_Adder_out_26[5]), .out_22(Ripple_Adder_out_26[4]),
    .out_23(Ripple_Adder_out_26[3]), .out_24(Ripple_Adder_out_26[2]), .out_25(Ripple_Adder_out_26[1]),
    .out_26(Ripple_Adder_out_26[0]), .C_IN(Carry_In));
  assign {out_25, out_26, out_27, out_28, out_29, out_30, out_31, out_32} = n2_to_4_decoder_1_out_7 ? Ripple_Adder_out_26 : 8'bz;  // Controlled_Buffer controlled_buffer_9

  // Notes on the sheet:
  //   Input B
  //   Input A
endmodule

module _2__to_4_Decoder (
  input  A,
  input  B,
  input  ENABLE,
  output out_4,
  output out_5,
  output out_6,
  output out_7
);

  wire not_1_out, not_2_out;

  not not_1 (not_1_out, A);
  not not_2 (not_2_out, B);
  and and_1 (out_4, not_1_out, not_2_out, ENABLE);
  and and_2 (out_5, A, not_2_out, ENABLE);
  and and_3 (out_6, B, not_1_out, ENABLE);
  and and_4 (out_7, B, A, ENABLE);
endmodule
