// Logisim project DLL9.circ as structural Verilog: 1 circuit, main circuit main
module main (
  input  [7:0] In_from_data_bus,
  input  CLK,
  input  Fetch,
  input  MAR,
  input  MDR,
  input  PC,
  input  MBR,
  input  SP,
  input  LV,
  input  CPP,
  input  TOS,
  input  OPC,
  input  H,
  input  ENB,
  input  ENA,
  input  INVA,
  input  Cin,
  input  F1,
  input  F0,
  input  [2:0] B_Bus,
  input  LRS,
  input  EnS,
  output [7:0] Address_Bus,
  output [7:0] Data_Bus,
  output Cout
);

  wire and_1_out, and_2_out, and_3_out, and_4_out, and_5_out, and_6_out, and_7_out, and_8_out, and_9_out,
       and_10_out, decoder_1_out0, decoder_1_out1, decoder_1_out2, decoder_1_out3, decoder_1_out4,
       decoder_1_out5, decoder_1_out6, decoder_1_out7, not_1_out, not_2_out;
  wire [7:0] alu_1_out_32, controlled_buffer_1_out, controlled_buffer_3_out, controlled_buffer_4_out,
       controlled_buffer_5_out, controlled_buffer_6_out, controlled_buffer_7_out, controlled_buffer_8_out,
       controlled_buffer_9_out, controlled_buffer_10_out, controlled_buffer_11_out, controlled_buffer_12_out,
       controlled_buffer_13_out, controlled_buffer_14_out, controlled_buffer_22_out, CPP_q0, H_q0, LV_q0,
       MBR_q0, n8_bit_wide_1_bit_left_right_shifter_1_s7, OPC_q0, PC_q0, SP_q0, TOS_q0;

  assign controlled_buffer_1_out = Fetch ? In_from_data_bus : 8'bz;  // Controlled_Buffer controlled_buffer_1
  assign controlled_buffer_1_out = not_1_out ? controlled_buffer_13_out : 8'bz;  // Controlled_Buffer controlled_buffer_2
  not not_1 (not_1_out, Fetch);
  and and_1 (and_1_out, CLK, MAR);
  assign controlled_buffer_3_out = and_1_out ? controlled_buffer_13_out : 8'bz;  // Controlled_Buffer controlled_buffer_3
  assign controlled_buffer_4_out = and_2_out ? controlled_buffer_1_out : 8'bz;  // Controlled_Buffer controlled_buffer_4
  and and_2 (and_2_out, CLK, MDR);
  assign controlled_buffer_5_out = and_4_out ? controlled_buffer_13_out : 8'bz;  // Controlled_Buffer controlled_buffer_5
  assign controlled_buffer_6_out = and_3_out ? controlled_buffer_13_out : 8'bz;  // Controlled_Buffer controlled_buffer_6
  assign controlled_buffer_7_out = and_5_out ? controlled_buffer_13_out : 8'bz;  // Controlled_Buffer controlled_buffer_7
  and and_3 (and_3_out, CLK, MBR);
  and and_4 (and_4_out, CLK, PC);
  assign controlled_buffer_8_out = and_6_out ? controlled_buffer_13_out : 8'bz;  // Controlled_Buffer controlled_buffer_8
  assign controlled_buffer_9_out = and_7_out ? controlled_buffer_13_out : 8'bz;  // Controlled_Buffer controlled_buffer_9
  assign controlled_buffer_10_out = and_8_out ? controlled_buffer_13_out : 8'bz;  // Controlled_Buffer controlled_buffer_10
  assign controlled_buffer_11_out = and_9_out ? controlled_buffer_13_out : 8'bz;  // Controlled_Buffer controlled_buffer_11
  and and_5 (and_5_out, CLK, SP);
  _8_bit_register u_MAR (
    .C(and_1_out), .D7(controlled_buffer_3_out[7]), .D6(controlled_buffer_3_out[6]),
    .D5(controlled_buffer_3_out[5]), .D4(controlled_buffer_3_out[4]), .D3(controlled_buffer_3_out[3]),
    .D2(controlled_buffer_3_out[2]), .D1(controlled_buffer_3_out[1]), .D0(controlled_buffer_3_out[0]),
    .Q7(Address_Bus[7]), .Q6(Address_Bus[6]), .Q5(Address_Bus[5]), .Q4(Address_Bus[4]), .Q3(Address_Bus[3]),
    .Q2(Address_Bus[2]), .Q1(Address_Bus[1]), .Q0(Address_Bus[0]));
  _8_bit_register u_MDR (
    .C(and_2_out), .D7(controlled_buffer_4_out[7]), .D6(controlled_buffer_4_out[6]),
    .D5(controlled_buffer_4_out[5]), .D4(controlled_buffer_4_out[4]), .D3(controlled_buffer_4_out[3]),
    .D2(controlled_buffer_4_out[2]), .D1(controlled_buffer_4_out[1]), .D0(controlled_buffer_4_out[0]),
    .Q7(Data_Bus[7]), .Q6(Data_Bus[6]), .Q5(Data_Bus[5]), .Q4(Data_Bus[4]), .Q3(Data_Bus[3]),
    .Q2(Data_Bus[2]), .Q1(Data_Bus[1]), .Q0(Data_Bus[0]));
  _8_bit_register u_PC (
    .C(and_4_out), .D7(controlled_buffer_5_out[7]), .D6(controlled_buffer_5_out[6]),
    .D5(controlled_buffer_5_out[5]), .D4(controlled_buffer_5_out[4]), .D3(controlled_buffer_5_out[3]),
    .D2(controlled_buffer_5_out[2]), .D1(controlled_buffer_5_out[1]), .D0(controlled_buffer_5_out[0]),
    .Q7(PC_q0[7]), .Q6(PC_q0[6]), .Q5(PC_q0[5]), .Q4(PC_q0[4]), .Q3(PC_q0[3]), .Q2(PC_q0[2]), .Q1(PC_q0[1]),
    .Q0(PC_q0[0]));
  _8_bit_register u_MBR (
    .C(and_3_out), .D7(controlled_buffer_6_out[7]), .D6(controlled_buffer_6_out[6]),
    .D5(controlled_buffer_6_out[5]), .D4(controlled_buffer_6_out[4]), .D3(controlled_buffer_6_out[3]),
    .D2(controlled_buffer_6_out[2]), .D1(controlled_buffer_6_out[1]), .D0(controlled_buffer_6_out[0]),
    .Q7(MBR_q0[7]), .Q6(MBR_q0[6]), .Q5(MBR_q0[5]), .Q4(MBR_q0[4]), .Q3(MBR_q0[3]), .Q2(MBR_q0[2]),
    .Q1(MBR_q0[1]), .Q0(MBR_q0[0]));
  _8_bit_register u_SP (
    .C(and_5_out), .D7(controlled_buffer_7_out[7]), .D6(controlled_buffer_7_out[6]),
    .D5(controlled_buffer_7_out[5]), .D4(controlled_buffer_7_out[4]), .D3(controlled_buffer_7_out[3]),
    .D2(controlled_buffer_7_out[2]), .D1(controlled_buffer_7_out[1]), .D0(controlled_buffer_7_out[0]),
    .Q7(SP_q0[7]), .Q6(SP_q0[6]), .Q5(SP_q0[5]), .Q4(SP_q0[4]), .Q3(SP_q0[3]), .Q2(SP_q0[2]), .Q1(SP_q0[1]),
    .Q0(SP_q0[0]));
  _8_bit_register u_LV (
    .C(and_6_out), .D7(controlled_buffer_8_out[7]), .D6(controlled_buffer_8_out[6]),
    .D5(controlled_buffer_8_out[5]), .D4(controlled_buffer_8_out[4]), .D3(controlled_buffer_8_out[3]),
    .D2(controlled_buffer_8_out[2]), .D1(controlled_buffer_8_out[1]), .D0(controlled_buffer_8_out[0]),
    .Q7(LV_q0[7]), .Q6(LV_q0[6]), .Q5(LV_q0[5]), .Q4(LV_q0[4]), .Q3(LV_q0[3]), .Q2(LV_q0[2]), .Q1(LV_q0[1]),
    .Q0(LV_q0[0]));
  _8_bit_register u_CPP (
    .C(and_7_out), .D7(controlled_buffer_9_out[7]), .D6(controlled_buffer_9_out[6]),
    .D5(controlled_buffer_9_out[5]), .D4(controlled_buffer_9_out[4]), .D3(controlled_buffer_9_out[3]),
    .D2(controlled_buffer_9_out[2]), .D1(controlled_buffer_9_out[1]), .D0(controlled_buffer_9_out[0]),
    .Q7(CPP_q0[7]), .Q6(CPP_q0[6]), .Q5(CPP_q0[5]), .Q4(CPP_q0[4]), .Q3(CPP_q0[3]), .Q2(CPP_q0[2]),
    .Q1(CPP_q0[1]), .Q0(CPP_q0[0]));
  _8_bit_register u_TOS (
    .C(and_8_out), .D7(controlled_buffer_10_out[7]), .D6(controlled_buffer_10_out[6]),
    .D5(controlled_buffer_10_out[5]), .D4(controlled_buffer_10_out[4]), .D3(controlled_buffer_10_out[3]),
    .D2(controlled_buffer_10_out[2]), .D1(controlled_buffer_10_out[1]), .D0(controlled_buffer_10_out[0]),
    .Q7(TOS_q0[7]), .Q6(TOS_q0[6]), .Q5(TOS_q0[5]), .Q4(TOS_q0[4]), .Q3(TOS_q0[3]), .Q2(TOS_q0[2]),
    .Q1(TOS_q0[1]), .Q0(TOS_q0[0]));
  _8_bit_register u_OPC (
    .C(and_9_out), .D7(controlled_buffer_11_out[7]), .D6(controlled_buffer_11_out[6]),
    .D5(controlled_buffer_11_out[5]), .D4(controlled_buffer_11_out[4]), .D3(controlled_buffer_11_out[3]),
    .D2(controlled_buffer_11_out[2]), .D1(controlled_buffer_11_out[1]), .D0(controlled_buffer_11_out[0]),
    .Q7(OPC_q0[7]), .Q6(OPC_q0[6]), .Q5(OPC_q0[5]), .Q4(OPC_q0[4]), .Q3(OPC_q0[3]), .Q2(OPC_q0[2]),
    .Q1(OPC_q0[1]), .Q0(OPC_q0[0]));
  assign controlled_buffer_12_out = and_10_out ? controlled_buffer_13_out : 8'bz;  // Controlled_Buffer controlled_buffer_12
  _8_bit_register u_H (
    .C(and_10_out), .D7(controlled_buffer_12_out[7]), .D6(controlled_buffer_12_out[6]),
    .D5(controlled_buffer_12_out[5]), .D4(controlled_buffer_12_out[4]), .D3(controlled_buffer_12_out[3]),
    .D2(controlled_buffer_12_out[2]), .D1(controlled_buffer_12_out[1]), .D0(controlled_buffer_12_out[0]),
    .Q7(H_q0[7]), .Q6(H_q0[6]), .Q5(H_q0[5]), .Q4(H_q0[4]), .Q3(H_q0[3]), .Q2(H_q0[2]), .Q1(H_q0[1]),
    .Q0(H_q0[0]));
  ALU alu_1 (
    .ENB(ENB), .ENA(ENA), .INVA(INVA), .Carry_In(Cin), .F1(F1), .Clk(CLK), .F0(F0),
    .B7(controlled_buffer_14_out[7]), .B6(controlled_buffer_14_out[6]), .B5(controlled_buffer_14_out[5]),
    .B4(controlled_buffer_14_out[4]), .B3(controlled_buffer_14_out[3]), .B2(controlled_buffer_14_out[2]),
    .B1(controlled_buffer_14_out[1]), .B0(controlled_buffer_14_out[0]), .A7(H_q0[7]), .A6(H_q0[6]),
    .A5(H_q0[5]), .A4(H_q0[4]), .A3(H_q0[3]), .A2(H_q0[2]), .A1(H_q0[1]), .A0(H_q0[0]),
    .out_25(alu_1_out_32[7]), .out_26(alu_1_out_32[6]), .out_27(alu_1_out_32[5]), .out_28(alu_1_out_32[4]),
    .out_29(alu_1_out_32[3]), .out_30(alu_1_out_32[2]), .out_31(alu_1_out_32[1]), .out_32(alu_1_out_32[0]),
    .Carry_Out(Cout));
  and and_6 (and_6_out, CLK, LV);
  and and_7 (and_7_out, CLK, CPP);
  and and_8 (and_8_out, CLK, TOS);
  and and_9 (and_9_out, CLK, OPC);
  assign controlled_buffer_13_out = not_2_out ? alu_1_out_32 : 8'bz;  // Controlled_Buffer controlled_buffer_13
  and and_10 (and_10_out, CLK, H);
  assign controlled_buffer_14_out = decoder_1_out0 ? Data_Bus : 8'bz;  // Controlled_Buffer controlled_buffer_14
  assign controlled_buffer_14_out = decoder_1_out1 ? PC_q0 : 8'bz;  // Controlled_Buffer controlled_buffer_15
  assign controlled_buffer_14_out = decoder_1_out2 ? MBR_q0 : 8'bz;  // Controlled_Buffer controlled_buffer_16
  assign controlled_buffer_14_out = decoder_1_out3 ? SP_q0 : 8'bz;  // Controlled_Buffer controlled_buffer_17
  assign controlled_buffer_14_out = decoder_1_out4 ? LV_q0 : 8'bz;  // Controlled_Buffer controlled_buffer_18
  assign controlled_buffer_14_out = decoder_1_out5 ? CPP_q0 : 8'bz;  // Controlled_Buffer controlled_buffer_19
  assign controlled_buffer_14_out = decoder_1_out6 ? TOS_q0 : 8'bz;  // Controlled_Buffer controlled_buffer_20
  assign controlled_buffer_14_out = decoder_1_out7 ? OPC_q0 : 8'bz;  // Controlled_Buffer controlled_buffer_21
  assign controlled_buffer_22_out = EnS ? alu_1_out_32 : 8'bz;  // Controlled_Buffer controlled_buffer_22
  not not_2 (not_2_out, EnS);
  assign controlled_buffer_13_out = EnS ? n8_bit_wide_1_bit_left_right_shifter_1_s7 : 8'bz;  // Controlled_Buffer controlled_buffer_23
  _8_bit_wide__1_bit_left_right_shifter u_8_bit_wide_1_bit_left_right_shifter_1 (
    .in_9(LRS), .D0(controlled_buffer_22_out[7]), .D1(controlled_buffer_22_out[6]),
    .D2(controlled_buffer_22_out[5]), .D3(controlled_buffer_22_out[4]), .D4(controlled_buffer_22_out[3]),
    .D5(controlled_buffer_22_out[2]), .D6(controlled_buffer_22_out[1]), .D7(controlled_buffer_22_out[0]),
    .S0(n8_bit_wide_1_bit_left_right_shifter_1_s7[7]), .S1(n8_bit_wide_1_bit_left_right_shifter_1_s7[6]),
    .S2(n8_bit_wide_1_bit_left_right_shifter_1_s7[5]), .S3(n8_bit_wide_1_bit_left_right_shifter_1_s7[4]),
    .S4(n8_bit_wide_1_bit_left_right_shifter_1_s7[3]), .S5(n8_bit_wide_1_bit_left_right_shifter_1_s7[2]),
    .S6(n8_bit_wide_1_bit_left_right_shifter_1_s7[1]), .S7(n8_bit_wide_1_bit_left_right_shifter_1_s7[0]));
  Decoder #(.select(3)) decoder_1 (
    .out0(decoder_1_out0), .out1(decoder_1_out1), .out2(decoder_1_out2), .out3(decoder_1_out3),
    .out4(decoder_1_out4), .out5(decoder_1_out5), .out6(decoder_1_out6), .out7(decoder_1_out7), .sel(B_Bus),
    .en(CLK));

  // Notes on the sheet:
  //   Data or C bus 
  //   to MDR control
  //   MAR
  //   MDR
  //   PC
  //   SP
  //   LV
  //   CPP
  //   TOS
  //   OPC
  //   H
  //   MBR
  //   Shifter en/dis
endmodule
