// Logisim project AdderCircuits.circ as structural Verilog
module HalfAdder (
  input  in_1,
  input  in_2,
  output out_3,
  output out_4
);

  xor xor_1 (out_3, in_1, in_2);
  buf and_1 (out_4, in_1);  // AND_Gate
endmodule

module FullAdder (
  input  A,
  input  B,
  input  C,
  output S,
  output C_OUT
);

  wire and_1_out, and_2_out, xor_1_out;

  xor xor_1 (xor_1_out, A, B);
  xor xor_2 (S, xor_1_out, C);
  and and_1 (and_1_out, xor_1_out, C);
  and and_2 (and_2_out, A, B);
  or or_1 (C_OUT, and_1_out, and_2_out);
endmodule

module _8bitRippleCarryAdder (
  input  A7,
  input  B7,
  input  A6,
  input  B6,
  input  A5,
  input  B5,
  input  A4,
  input  B4,
  input  A3,
  input  B3,
  input  A2,
  input  B2,
  input  A1,
  input  B1,
  input  A0,
  input  B0,
  output out_17,
  output out_18,
  output out_19,
  output out_20,
  output out_21,
  output out_22,
  output out_23,
  output out_24
);

  wire fulladder_1_c_out, fulladder_2_c_out, fulladder_3_c_out, fulladder_4_c_out, fulladder_5_c_out,
       fulladder_6_c_out, fulladder_7_c_out, halfadder_1_out_4;

  FullAdder fulladder_1 (.A(B7), .B(A7), .C(fulladder_2_c_out), .S(out_17), .C_OUT(fulladder_1_c_out));
  FullAdder fulladder_2 (.A(B6), .B(A6), .C(fulladder_3_c_out), .S(out_18), .C_OUT(fulladder_2_c_out));
  FullAdder fulladder_3 (.A(B5), .B(A5), .C(fulladder_4_c_out), .S(out_19), .C_OUT(fulladder_3_c_out));
  FullAdder fulladder_4 (.A(B4), .B(A4), .C(fulladder_5_c_out), .S(out_20), .C_OUT(fulladder_4_c_out));
  FullAdder fulladder_5 (.A(B3), .B(A3), .C(fulladder_6_c_out), .S(out_21), .C_OUT(fulladder_5_c_out));
  FullAdder fulladder_6 (.A(B2), .B(A2), .C(fulladder_7_c_out), .S(out_22), .C_OUT(fulladder_6_c_out));
  FullAdder fulladder_7 (.A(B1), .B(A1), .C(halfadder_1_out_4), .S(out_23), .C_OUT(fulladder_7_c_out));
  HalfAdder halfadder_1 (.in_1(B0), .in_2(A0), .out_3(out_24), .out_4(halfadder_1_out_4));
endmodule
