// Logisim project Latches.circ as structural Verilog
module SR_Latch (
  input  in_1,
  input  in_2,
  output Q,
  output Q_2
);

  nand nand_1 (Q, in_1, Q_2);
  nand nand_2 (Q_2, Q, in_2);

  // Notes on the sheet:
  //   _
endmodule

module SR_Flip_Flop (
  input  S,
  input  CK,
  input  R,
  output Q,
  output Q_2
);

  wire nand_1_out, nand_2_out;

  nand nand_1 (nand_1_out, S, CK);
  nand nand_2 (nand_2_out, CK, R);
  SR_Latch sr_latch_1 (.in_1(nand_1_out), .in_2(nand_2_out), .Q(Q), .Q_2(Q_2));

  // Notes on the sheet:
  //   _
endmodule

module D_Flip_Flop (
  input  D,
  input  CLK,
  output Q,
  output Q_2
);

  wire nand_1_out, nand_2_out, not_1_out;

  not not_1 (not_1_out, D);
  nand nand_1 (nand_1_out, D, CLK);
  nand nand_2 (nand_2_out, not_1_out, CLK);
  SR_Latch sr_latch_1 (.in_1(nand_1_out), .in_2(nand_2_out), .Q(Q), .Q_2(Q_2));

  // Notes on the sheet:
  //   _
endmodule

module _8_bit_register (
  input  D7,
  input  D7_2,
  input  D7_3,
  input  D7_4,
  input  D7_5,
  input  D7_6,
  input  D7_7,
  input  D7_8,
  input  C,
  output Q7,
  output Q7_2,
  output Q7_3,
  output Q7_4,
  output Q7_5,
  output Q7_6,
  output Q7_7,
  output Q7_8
);

  D_Flip_Flop d_ff_1 (.D(D7), .CLK(C), .Q(Q7));  // open: Q_2
  D_Flip_Flop d_ff_2 (.D(D7_2), .CLK(C), .Q(Q7_2));  // open: Q_2
  D_Flip_Flop d_ff_3 (.D(D7_3), .CLK(C), .Q(Q7_3));  // open: Q_2
  D_Flip_Flop d_ff_4 (.D(D7_4), .CLK(C), .Q(Q7_4));  // open: Q_2
  D_Flip_Flop d_ff_5 (.D(D7_5), .CLK(C), .Q(Q7_5));  // open: Q_2
  D_Flip_Flop d_ff_6 (.D(D7_6), .CLK(C), .Q(Q7_6));  // open: Q_2
  D_Flip_Flop d_ff_7 (.D(D7_7), .CLK(C), .Q(Q7_7));  // open: Q_2
  D_Flip_Flop d_ff_8 (.D(D7_8), .CLK(C), .Q(Q7_8));  // open: Q_2
endmodule

module Binary_Memory_Cell (
  input  Select,
  input  Data_In,
  input  Read____Write_0,
  output Data_Out
);

  wire and_1_out, and_2_out, not_1_out, not_2_out, not_3_out, not_4_out, sr_latch_1_q;

  not not_1 (not_1_out, Data_In);
  and and_1 (and_1_out, Select, Data_In, not_2_out);
  and and_2 (and_2_out, Select, not_1_out, not_2_out);
  not not_2 (not_2_out, Read____Write_0);
  not not_3 (not_3_out, and_1_out);
  not not_4 (not_4_out, and_2_out);
  SR_Latch sr_latch_1 (.in_1(not_3_out), .in_2(not_4_out), .Q(sr_latch_1_q));  // open: Q_2
  and and_3 (Data_Out, Select, sr_latch_1_q, Read____Write_0);

  // Notes on the sheet:
  //   S
  //   R
  //   SR Latch
  //   Q
endmodule

module Single_Bit_Memory_Cell_Showing_connection_to_control_bus_and_bi_directional_data_bus (
  input  Data_Bus_Input,
  input  [1:0] Control_bus_Input,
  output Data_Bus_State,
  output [1:0] Control_Line_State
);

  wire binary_memory_cell_1_data_out, controlled_buffer_2_out, not_1_out;

  assign Data_Bus_State = not_1_out ? Data_Bus_Input : 1'bz;  // Controlled_Buffer controlled_buffer_1
  not not_1 (not_1_out, Control_bus_Input[1]);
  assign controlled_buffer_2_out = not_1_out ? Data_Bus_State : 1'bz;  // Controlled_Buffer controlled_buffer_2
  Binary_Memory_Cell binary_memory_cell_1 (
    .Data_In(controlled_buffer_2_out), .Select(Control_bus_Input[0]), .Read____Write_0(Control_bus_Input[1]),
    .Data_Out(binary_memory_cell_1_data_out));
  assign Data_Bus_State = Control_bus_Input[1] ? binary_memory_cell_1_data_out : 1'bz;  // Controlled_Buffer controlled_buffer_3

  assign Control_Line_State = Control_bus_Input;
endmodule

module _8_bit_Binay_Memory_Cell (
  input  Enable,
  input  Read_1___Write_0,
  input  in_3,
  input  in_4,
  input  in_5,
  input  in_6,
  input  in_7,
  input  in_8,
  input  in_9,
  input  in_10,
  output out_11,
  output out_12,
  output out_13,
  output out_14,
  output out_15,
  output out_16,
  output out_17,
  output out_18
);

  Binary_Memory_Cell binary_memory_cell_1 (
    .Data_In(in_3), .Select(Enable), .Read____Write_0(Read_1___Write_0), .Data_Out(out_11));
  Binary_Memory_Cell binary_memory_cell_2 (
    .Data_In(in_4), .Select(Enable), .Read____Write_0(Read_1___Write_0), .Data_Out(out_12));
  Binary_Memory_Cell binary_memory_cell_3 (
    .Data_In(in_5), .Select(Enable), .Read____Write_0(Read_1___Write_0), .Data_Out(out_13));
  Binary_Memory_Cell binary_memory_cell_4 (
    .Data_In(in_6), .Select(Enable), .Read____Write_0(Read_1___Write_0), .Data_Out(out_14));
  Binary_Memory_Cell binary_memory_cell_5 (
    .Data_In(in_7), .Select(Enable), .Read____Write_0(Read_1___Write_0), .Data_Out(out_15));
  Binary_Memory_Cell binary_memory_cell_6 (
    .Data_In(in_8), .Select(Enable), .Read____Write_0(Read_1___Write_0), .Data_Out(out_16));
  Binary_Memory_Cell binary_memory_cell_7 (
    .Data_In(in_9), .Select(Enable), .Read____Write_0(Read_1___Write_0), .Data_Out(out_17));
  Binary_Memory_Cell binary_memory_cell_8 (
    .Data_In(in_10), .Select(Enable), .Read____Write_0(Read_1___Write_0), .Data_Out(out_18));
endmodule

module _4_Byte_Address_Memory_Chip (
  input  [7:0] in_1,
  input  [7:0] in_2,
  input  [1:0] in_3,
  output [7:0] out_4,
  output [7:0] out_5,
  output [1:0] out_6
);

  wire and_1_out, and_2_out, n2_4_decoder_1_out_4, n2_4_decoder_1_out_5, n2_4_decoder_1_out_6,
       n2_4_decoder_1_out_7, n8_bit_binay_memory_cell_1_out_11, n8_bit_binay_memory_cell_1_out_12,
       n8_bit_binay_memory_cell_1_out_13, n8_bit_binay_memory_cell_1_out_14,
       n8_bit_binay_memory_cell_1_out_15, n8_bit_binay_memory_cell_1_out_16,
       n8_bit_binay_memory_cell_1_out_17, n8_bit_binay_memory_cell_1_out_18,
       n8_bit_binay_memory_cell_2_out_11, n8_bit_binay_memory_cell_2_out_12,
       n8_bit_binay_memory_cell_2_out_13, n8_bit_binay_memory_cell_2_out_14,
       n8_bit_binay_memory_cell_2_out_15, n8_bit_binay_memory_cell_2_out_16,
       n8_bit_binay_memory_cell_2_out_17, n8_bit_binay_memory_cell_2_out_18,
       n8_bit_binay_memory_cell_3_out_11, n8_bit_binay_memory_cell_3_out_12,
       n8_bit_binay_memory_cell_3_out_13, n8_bit_binay_memory_cell_3_out_14,
       n8_bit_binay_memory_cell_3_out_15, n8_bit_binay_memory_cell_3_out_16,
       n8_bit_binay_memory_cell_3_out_17, n8_bit_binay_memory_cell_3_out_18,
       n8_bit_binay_memory_cell_4_out_11, n8_bit_binay_memory_cell_4_out_12,
       n8_bit_binay_memory_cell_4_out_13, n8_bit_binay_memory_cell_4_out_14,
       n8_bit_binay_memory_cell_4_out_15, n8_bit_binay_memory_cell_4_out_16,
       n8_bit_binay_memory_cell_4_out_17, n8_bit_binay_memory_cell_4_out_18, not_1_out, not_2_out, or_1_out;
  wire [7:0] controlled_buffer_2_out, D0_out;

  not not_1 (not_1_out, or_1_out);
  _2_4_Decoder u_2_4_decoder_1 (
    .A(in_2[1]), .B(in_2[0]), .ENABLE(and_1_out), .out_4(n2_4_decoder_1_out_4), .out_5(n2_4_decoder_1_out_5),
    .out_6(n2_4_decoder_1_out_6), .out_7(n2_4_decoder_1_out_7));
  and and_1 (and_1_out, not_1_out, in_3[1]);
  and and_2 (and_2_out, in_3[0], in_3[1]);
  or or_1 (or_1_out, in_2[7], in_2[6], in_2[5], in_2[4], in_2[3], in_2[2]);
  assign out_4 = not_2_out ? in_1 : 8'bz;  // Controlled_Buffer controlled_buffer_1
  assign controlled_buffer_2_out = not_2_out ? out_4 : 8'bz;  // Controlled_Buffer controlled_buffer_2
  not not_2 (not_2_out, and_2_out);
  _8_bit_Binay_Memory_Cell u_8_bit_binay_memory_cell_1 (
    .in_3(controlled_buffer_2_out[7]), .in_4(controlled_buffer_2_out[6]), .in_5(controlled_buffer_2_out[5]),
    .in_6(controlled_buffer_2_out[4]), .in_7(controlled_buffer_2_out[3]), .in_8(controlled_buffer_2_out[2]),
    .in_9(controlled_buffer_2_out[1]), .in_10(controlled_buffer_2_out[0]), .Enable(n2_4_decoder_1_out_4),
    .Read_1___Write_0(in_3[0]), .out_11(n8_bit_binay_memory_cell_1_out_11),
    .out_12(n8_bit_binay_memory_cell_1_out_12), .out_13(n8_bit_binay_memory_cell_1_out_13),
    .out_14(n8_bit_binay_memory_cell_1_out_14), .out_15(n8_bit_binay_memory_cell_1_out_15),
    .out_16(n8_bit_binay_memory_cell_1_out_16), .out_17(n8_bit_binay_memory_cell_1_out_17),
    .out_18(n8_bit_binay_memory_cell_1_out_18));
  _8_bit_Binay_Memory_Cell u_8_bit_binay_memory_cell_2 (
    .in_3(controlled_buffer_2_out[7]), .in_4(controlled_buffer_2_out[6]), .in_5(controlled_buffer_2_out[5]),
    .in_6(controlled_buffer_2_out[4]), .in_7(controlled_buffer_2_out[3]), .in_8(controlled_buffer_2_out[2]),
    .in_9(controlled_buffer_2_out[1]), .in_10(controlled_buffer_2_out[0]), .Enable(n2_4_decoder_1_out_5),
    .Read_1___Write_0(in_3[0]), .out_11(n8_bit_binay_memory_cell_2_out_11),
    .out_12(n8_bit_binay_memory_cell_2_out_12), .out_13(n8_bit_binay_memory_cell_2_out_13),
    .out_14(n8_bit_binay_memory_cell_2_out_14), .out_15(n8_bit_binay_memory_cell_2_out_15),
    .out_16(n8_bit_binay_memory_cell_2_out_16), .out_17(n8_bit_binay_memory_cell_2_out_17),
    .out_18(n8_bit_binay_memory_cell_2_out_18));
  _8_bit_Binay_Memory_Cell u_8_bit_binay_memory_cell_3 (
    .in_3(controlled_buffer_2_out[7]), .in_4(controlled_buffer_2_out[6]), .in_5(controlled_buffer_2_out[5]),
    .in_6(controlled_buffer_2_out[4]), .in_7(controlled_buffer_2_out[3]), .in_8(controlled_buffer_2_out[2]),
    .in_9(controlled_buffer_2_out[1]), .in_10(controlled_buffer_2_out[0]), .Enable(n2_4_decoder_1_out_6),
    .Read_1___Write_0(in_3[0]), .out_11(n8_bit_binay_memory_cell_3_out_11),
    .out_12(n8_bit_binay_memory_cell_3_out_12), .out_13(n8_bit_binay_memory_cell_3_out_13),
    .out_14(n8_bit_binay_memory_cell_3_out_14), .out_15(n8_bit_binay_memory_cell_3_out_15),
    .out_16(n8_bit_binay_memory_cell_3_out_16), .out_17(n8_bit_binay_memory_cell_3_out_17),
    .out_18(n8_bit_binay_memory_cell_3_out_18));
  _8_bit_Binay_Memory_Cell u_8_bit_binay_memory_cell_4 (
    .in_3(controlled_buffer_2_out[7]), .in_4(controlled_buffer_2_out[6]), .in_5(controlled_buffer_2_out[5]),
    .in_6(controlled_buffer_2_out[4]), .in_7(controlled_buffer_2_out[3]), .in_8(controlled_buffer_2_out[2]),
    .in_9(controlled_buffer_2_out[1]), .in_10(controlled_buffer_2_out[0]), .Enable(n2_4_decoder_1_out_7),
    .Read_1___Write_0(in_3[0]), .out_11(n8_bit_binay_memory_cell_4_out_11),
    .out_12(n8_bit_binay_memory_cell_4_out_12), .out_13(n8_bit_binay_memory_cell_4_out_13),
    .out_14(n8_bit_binay_memory_cell_4_out_14), .out_15(n8_bit_binay_memory_cell_4_out_15),
    .out_16(n8_bit_binay_memory_cell_4_out_16), .out_17(n8_bit_binay_memory_cell_4_out_17),
    .out_18(n8_bit_binay_memory_cell_4_out_18));
  or D7 (D0_out[7], n8_bit_binay_memory_cell_4_out_18, n8_bit_binay_memory_cell_3_out_18, n8_bit_binay_memory_cell_2_out_18, n8_bit_binay_memory_cell_1_out_18);
  or D6 (D0_out[6], n8_bit_binay_memory_cell_4_out_17, n8_bit_binay_memory_cell_3_out_17, n8_bit_binay_memory_cell_2_out_17, n8_bit_binay_memory_cell_1_out_17);
  or D5 (D0_out[5], n8_bit_binay_memory_cell_4_out_16, n8_bit_binay_memory_cell_3_out_16, n8_bit_binay_memory_cell_2_out_16, n8_bit_binay_memory_cell_1_out_16);
  or D4 (D0_out[4], n8_bit_binay_memory_cell_4_out_15, n8_bit_binay_memory_cell_3_out_15, n8_bit_binay_memory_cell_2_out_15, n8_bit_binay_memory_cell_1_out_15);
  or D3 (D0_out[3], n8_bit_binay_memory_cell_4_out_14, n8_bit_binay_memory_cell_3_out_14, n8_bit_binay_memory_cell_2_out_14, n8_bit_binay_memory_cell_1_out_14);
  assign out_4 = and_2_out ? D0_out : 8'bz;  // Controlled_Buffer controlled_buffer_3
  or D1 (D0_out[1], n8_bit_binay_memory_cell_4_out_12, n8_bit_binay_memory_cell_3_out_12, n8_bit_binay_memory_cell_2_out_12, n8_bit_binay_memory_cell_1_out_12);
  or D2 (D0_out[2], n8_bit_binay_memory_cell_4_out_13, n8_bit_binay_memory_cell_3_out_13, n8_bit_binay_memory_cell_2_out_13, n8_bit_binay_memory_cell_1_out_13);
  or D0 (D0_out[0], n8_bit_binay_memory_cell_4_out_11, n8_bit_binay_memory_cell_3_out_11, n8_bit_binay_memory_cell_2_out_11, n8_bit_binay_memory_cell_1_out_11);

  assign out_5 = in_2;
  assign out_6 = in_3;
endmodule

module _2_4_Decoder (
  input  A,
  input  B,
  input  ENABLE,
  output out_4,
  output out_5,
  output out_6,
  output out_7
);

  wire not_1_out, not_2_out;

  not not_1 (not_1_out, A);
  not not_2 (not_2_out, B);
  and _00 (out_4, not_1_out, not_2_out, ENABLE);
  and _10 (out_5, A, not_2_out, ENABLE);
  and _01 (out_6, B, not_1_out, ENABLE);
  and _11 (out_7, B, A, ENABLE);
endmodule
